# Fritzing sketch SigGen (saved by Fritzing 0.9.3b)

parts:
  Part2 = Adafruit Si5351A Clock Generator [part_number="Adafruit #2045"]
  ENCODER1 = Rotary Encoder with Knob
  Part1 = Arduino Nano (Rev3.0)
  Part3 = Adafruit I2C+SPI LCD Backpack [part_number="Adafruit #292"]
  U1 = LCD-16X2 [package=lcd-16x2]
  BAT1 = BC9VPC [package=bc9vpc]

nets:
  VIN: Part2.VIN, Part1.5V, Part3.VCC, U1.VDD, U1.A
  GND: Part2.GND, ENCODER1.no_name_yet#3, ENCODER1.no_name_yet#5, Part1.GND, Part3.GND, U1.VSS, U1.R_W, BAT1.V-
  N1: Part2.SDA, Part1.A4, Part3.DATA
  N2: Part2.SCL, Part1.A5, Part3.CLOCK
  N3: ENCODER1.no_name_yet#1, Part1.D3
  N4: ENCODER1.no_name_yet#2, Part1.D2
  N5: ENCODER1.no_name_yet#4, Part1.D4
  N6: Part1.VIN, BAT1.V+
  N7: Part3.CONTRAST, U1.VO
  N8: Part3.RS, U1.RS
  N9: Part3.E, U1.E
  N10: Part3.DB0, U1.DB0
  N11: Part3.DB1, U1.DB1
  N12: Part3.DB2, U1.DB2
  N13: Part3.DB3, U1.DB3
  N14: Part3.DB4, U1.DB4
  N15: Part3.DB5, U1.DB5
  N16: Part3.DB6, U1.DB6
  N17: Part3.DB7, U1.DB7
  N18: Part3.LEDK, U1.K

custom parts:
  Adafruit Si5351A Clock Generator: Never hunt around for another crystal again, with the Si5351A clock generator breakout from Adafruit! This chip has a precision 25MHz crystal reference and internal PLL and dividers so it can generate just about any frequency, from <8KHz up to 150+ MHz. The Si5351A clock generator is an I2C controller clock generator. It uses the onboard precision clock to drive multiple PLL's and clock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
  Rotary Encoder with Knob: Rotary Encoder with 1/4" Shaft and Knob
  Adafruit I2C+SPI LCD Backpack: LCD backpacks reduce the number of pins needed to connect to an LCD. LCDs are a fun and easy way to have your microcontroller project talk back to you. Character LCDs are common, and easy to get, available in tons of colors and sizes. We've written tutorials on using character LCDs with an Arduino (or similar microcontroller) but find that the number of pins necessary to control the LCD can be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
